// Logisim project Contador macabro ej 4-5.circ as structural Verilog: 2 circuits, main circuit main
module main (
  input  in_1,
  output out_2,
  output out_3,
  output out_4
);

  wire and_1_out, and_2_out, j_k_ff_2_qn, j_k_ff_3_qn;

  J_K_Flip_Flop j_k_ff_1 (.J(1'b1), .clk(in_1), .K(1'b1), .Q(out_2));  // open: Qn, preset, en, reset
  J_K_Flip_Flop j_k_ff_2 (
    .J(and_1_out), .clk(in_1), .K(out_2), .Q(out_3), .Qn(j_k_ff_2_qn));  // open: preset, en, reset
  J_K_Flip_Flop j_k_ff_3 (
    .J(out_2), .clk(in_1), .K(and_2_out), .Q(out_4), .Qn(j_k_ff_3_qn));  // open: preset, en, reset
  and and_1 (and_1_out, out_2, j_k_ff_3_qn);
  and and_2 (and_2_out, j_k_ff_2_qn, out_2);
endmodule

module contador_cabron (
  output out_1,
  output out_2,
  output out_3
);

  wire and_1_out, and_2_out, and_3_out, and_4_out, and_5_out, and_6_out, and_7_out, and_8_out, and_9_out,
       and_10_out, and_11_out, button_1_out, comparator_1_gt, j_k_ff_2_qn, j_k_ff_3_qn, not_1_out, not_2_out,
       not_3_out, or_1_out;
  wire [2:0] counter_1_q, multiplexer_1_out;

  Button button_1 (.out(button_1_out));
  and and_1 (and_1_out, or_1_out, multiplexer_1_out[2]);
  J_K_Flip_Flop j_k_ff_1 (
    .J(1'b1), .clk(button_1_out), .K(1'b1), .Q(out_1), .preset(and_1_out), .reset(and_2_out));  // open: Qn, en
  and and_2 (and_2_out, not_1_out, or_1_out);
  not not_1 (not_1_out, multiplexer_1_out[2]);
  and and_3 (and_3_out, or_1_out, multiplexer_1_out[1]);
  J_K_Flip_Flop j_k_ff_2 (
    .J(and_7_out), .clk(button_1_out), .K(out_1), .Q(out_2), .Qn(j_k_ff_2_qn), .preset(and_3_out),
    .reset(and_4_out));  // open: en
  and and_4 (and_4_out, not_2_out, or_1_out);
  not not_2 (not_2_out, multiplexer_1_out[1]);
  J_K_Flip_Flop j_k_ff_3 (
    .J(out_1), .clk(button_1_out), .K(and_8_out), .Q(out_3), .Qn(j_k_ff_3_qn), .preset(and_5_out),
    .reset(and_6_out));  // open: en
  and and_5 (and_5_out, or_1_out, multiplexer_1_out[0]);
  and and_6 (and_6_out, not_3_out, or_1_out);
  not not_3 (not_3_out, multiplexer_1_out[0]);
  and and_7 (and_7_out, out_1, j_k_ff_3_qn);
  and and_8 (and_8_out, j_k_ff_2_qn, out_1);
  and and_9 (and_9_out, ~out_1, ~out_2, ~out_3);  // AND_Gate
  and and_10 (and_10_out, and_9_out, comparator_1_gt);
  and and_11 (and_11_out, out_1, ~out_2, ~out_3);  // AND_Gate
  or or_1 (or_1_out, and_10_out, and_11_out);
  Multiplexer #(.select(3), .width(3)) multiplexer_1 (
    .in0(3'b011), .in1(3'b011), .in2(3'b111), .in3(3'b001), .in4(3'b101), .out(multiplexer_1_out),
    .sel(counter_1_q));  // open: in5, in6, in7, en
  Counter #(.width(3), .max('h4)) counter_1 (.Q(counter_1_q), .clk(or_1_out));  // open: load, D, count, carry, clr
  Comparator #(.width(3), .mode("unsigned")) comparator_1 (
    .a(counter_1_q), .b(3'b000), .gt(comparator_1_gt));  // open: eq, lt
endmodule
