// Logisim project Motor ej 2.circ as structural Verilog: 1 circuit, main circuit main
module main (
  input  [1:0] in_1,
  output out_2
);

  wire and_1_out, and_2_out, and_3_out, and_4_out, and_5_out, and_6_out, button_1_out, d_ff_1_qn, d_ff_2_q,
       d_ff_2_qn, not_1_out, not_2_out, or_1_out, or_2_out;

  Button button_1 (.out(button_1_out));
  not not_1 (not_1_out, in_1[0]);
  not not_2 (not_2_out, in_1[1]);
  D_Flip_Flop d_ff_1 (.clk(button_1_out), .D(or_1_out), .Q(out_2), .Qn(d_ff_1_qn));  // open: preset, en, reset
  D_Flip_Flop d_ff_2 (.clk(button_1_out), .D(or_2_out), .Q(d_ff_2_q), .Qn(d_ff_2_qn));  // open: preset, en, reset
  and and_1 (and_1_out, d_ff_1_qn, d_ff_2_q, not_1_out, not_2_out);
  and and_2 (and_2_out, out_2, in_1[0]);
  and and_3 (and_3_out, out_2, in_1[1]);
  and and_4 (and_4_out, out_2, d_ff_2_qn);
  and and_5 (and_5_out, out_2, in_1[0]);
  and and_6 (and_6_out, d_ff_1_qn, in_1[1]);
  or or_1 (or_1_out, and_1_out, and_2_out, and_3_out, and_4_out);
  or or_2 (or_2_out, and_5_out, and_6_out);
endmodule
