// Logisim project Secuencia.circ as structural Verilog: 2 circuits, main circuit main
module main (
  input  in_1,
  input  in_2,
  input  in_3,
  input  in_4,
  input  in_5,
  input  [1:0] in_6,
  input  in_7,
  output out_8,
  output out_9,
  output out_10,
  output out_11
);

  wire multiplexer_1_out, multiplexer_2_out, multiplexer_3_out, multiplexer_4_out;

  Multiplexer #(.select(2)) multiplexer_1 (
    .in0(out_8), .in1(out_11), .in2(out_9), .in3(in_2), .out(multiplexer_1_out), .sel(in_6));  // open: en
  D_Flip_Flop d_ff_1 (.clk(in_1), .D(multiplexer_1_out), .Q(out_8), .reset(in_7));  // open: Qn, preset, en
  Multiplexer #(.select(2)) multiplexer_2 (
    .in0(out_9), .in1(out_8), .in2(out_10), .in3(in_3), .out(multiplexer_2_out), .sel(in_6));  // open: en
  D_Flip_Flop d_ff_2 (.clk(in_1), .D(multiplexer_2_out), .Q(out_9), .reset(in_7));  // open: Qn, preset, en
  Multiplexer #(.select(2)) multiplexer_3 (
    .in0(out_10), .in1(out_9), .in2(out_11), .in3(in_4), .out(multiplexer_3_out), .sel(in_6));  // open: en
  D_Flip_Flop d_ff_3 (.clk(in_1), .D(multiplexer_3_out), .Q(out_10), .reset(in_7));  // open: Qn, preset, en
  Multiplexer #(.select(2)) multiplexer_4 (
    .in0(out_11), .in1(out_10), .in2(out_8), .in3(in_5), .out(multiplexer_4_out), .sel(in_6));  // open: en
  D_Flip_Flop d_ff_4 (.clk(in_1), .D(multiplexer_4_out), .Q(out_11), .reset(in_7));  // open: Qn, preset, en
endmodule

module secuencia (
  input  in_1,
  input  in_2,
  input  in_3,
  input  in_4,
  output out_5,
  output out_6,
  output out_7,
  output out_8
);

  wire and_1_out, button_1_out, not_1_out;
  wire [1:0] multiplexer_1_out;
  wire [2:0] counter_1_q;

  Button button_1 (.out(button_1_out));
  not not_1 (not_1_out, button_1_out);
  Counter #(.width(3), .max('h4)) counter_1 (.Q(counter_1_q), .clk(button_1_out));  // open: load, D, count, carry, clr
  Multiplexer #(.select(3), .width(2)) multiplexer_1 (
    .in0(2'b01), .in1(2'b11), .in2(2'b10), .in4(2'b11), .out(multiplexer_1_out), .sel(counter_1_q));  // open: in3, in5, in6, in7, en
  main main_1 (
    .in_1(not_1_out), .in_2(in_1), .in_3(in_2), .in_4(in_3), .in_5(in_4), .in_6(multiplexer_1_out),
    .in_7(and_1_out), .out_8(out_5), .out_9(out_6), .out_10(out_7), .out_11(out_8));
  and and_1 (and_1_out, counter_1_q[0], counter_1_q[1], ~counter_1_q[2]);  // AND_Gate
endmodule
