// Logisim project Comparador C1 C2 SM Ej 5.circ as structural Verilog: 1 circuit, main circuit main
module main (
  input  [3:0] A,
  input  [1:0] _00__SM,
  input  [3:0] B,
  output A_B,
  output A_B_2,
  output A_B_3
);

  wire and_1_out, and_3_out, and_4_out, and_5_out, and_6_out, and_7_out, comparator_1_gt, comparator_1_lt,
       not_1_out, not_2_out, not_3_out, not_4_out, or_1_out, or_2_out, or_3_out;
  wire [3:0] xor_1_out, xor_5_out;

  and and_1 (and_1_out, ~A[0], ~A[1], ~A[2], A[3], ~_00__SM[0], ~_00__SM[1]);  // AND_Gate
  or or_1 (or_1_out, and_1_out, and_1_out);
  and and_2 (and_1_out, A[0], A[1], A[2], A[3], _00__SM[0]);
  and and_3 (and_3_out, ~B[0], ~B[1], ~B[2], B[3], ~_00__SM[0], ~_00__SM[1]);  // AND_Gate
  or or_2 (or_2_out, and_3_out, and_4_out);
  and and_4 (and_4_out, B[0], B[1], B[2], B[3], _00__SM[0]);
  xor xor_1 (xor_1_out[0], A[0], and_1_out);
  xor xor_2 (xor_1_out[1], A[1], and_1_out);
  xor xor_3 (xor_1_out[2], A[2], and_1_out);
  xor xor_4 (xor_1_out[3], A[3], or_1_out);
  xor xor_5 (xor_5_out[0], B[0], and_4_out);
  xor xor_6 (xor_5_out[1], B[1], and_4_out);
  xor xor_7 (xor_5_out[2], B[2], and_4_out);
  xor xor_8 (xor_5_out[3], B[3], or_2_out);
  not not_1 (not_1_out, _00__SM[0]);
  not not_2 (not_2_out, _00__SM[1]);
  not not_3 (not_3_out, xor_1_out[3]);
  not not_4 (not_4_out, xor_5_out[3]);
  Comparator #(.width(4), .mode("unsigned")) comparator_1 (
    .a(xor_1_out), .b(xor_5_out), .gt(comparator_1_gt), .eq(A_B_2), .lt(comparator_1_lt));
  and and_5 (and_5_out, not_3_out, xor_5_out[3]);
  and and_6 (and_6_out, xor_1_out[3], not_4_out);
  and and_7 (and_7_out, xor_5_out[3], not_1_out, not_2_out);
  or or_3 (or_3_out, and_5_out, and_6_out, and_7_out);
  xor xor_9 (A_B, or_3_out, comparator_1_gt);
  xor xor_10 (A_B_3, or_3_out, comparator_1_lt);

  // Notes on the sheet:
  //   01->C1
  //   10->C2
endmodule
