// Logisim project Comparador C1 EJ 4.circ as structural Verilog: 1 circuit, main circuit main
module main (
  input  [3:0] in_1,
  input  [3:0] in_2,
  input  [3:0] in_3,
  output [3:0] out_4,
  output [1:0] out_5
);

  wire and_1_out, and_2_out, and_3_out, comparator_2_eq;
  wire [1:0] comparator_1_eq;
  wire [3:0] xor_1_out, xor_5_out, xor_9_out;

  and and_1 (and_1_out, in_1[0], in_1[1], in_1[2], in_1[3]);
  and and_2 (and_2_out, in_2[0], in_2[1], in_2[2], in_2[3]);
  and and_3 (and_3_out, in_3[0], in_3[1], in_3[2], in_3[3]);
  xor xor_1 (xor_1_out[0], and_1_out, in_1[0]);
  xor xor_2 (xor_1_out[1], and_1_out, in_1[1]);
  xor xor_3 (xor_1_out[2], and_1_out, in_1[2]);
  xor xor_4 (xor_1_out[3], and_1_out, in_1[3]);
  xor xor_5 (xor_5_out[0], and_2_out, in_2[0]);
  xor xor_6 (xor_5_out[1], and_2_out, in_2[1]);
  xor xor_7 (xor_5_out[2], and_2_out, in_2[2]);
  xor xor_8 (xor_5_out[3], and_2_out, in_2[3]);
  xor xor_9 (xor_9_out[0], and_3_out, in_3[0]);
  xor xor_10 (xor_9_out[1], and_3_out, in_3[1]);
  xor xor_11 (xor_9_out[2], and_3_out, in_3[2]);
  xor xor_12 (xor_9_out[3], and_3_out, in_3[3]);
  Comparator #(.width(4), .mode("unsigned")) comparator_1 (
    .a(xor_1_out), .b(xor_5_out), .eq(comparator_1_eq[0]));  // open: gt, lt
  Comparator #(.width(4), .mode("unsigned")) comparator_2 (
    .a(xor_1_out), .b(xor_9_out), .eq(comparator_2_eq));  // open: gt, lt
  Comparator #(.width(4), .mode("unsigned")) comparator_3 (
    .a(xor_5_out), .b(xor_9_out), .eq(comparator_1_eq[1]));  // open: gt, lt
  or or_1 (out_5[1], comparator_1_eq[0], comparator_2_eq, comparator_1_eq[1]);
  and and_4 (out_5[0], comparator_1_eq[0], comparator_2_eq);
  Multiplexer #(.select(2), .width(4)) multiplexer_1 (
    .in0(4'b0000), .in1(xor_1_out), .in2(xor_5_out), .in3(xor_1_out), .out(out_4), .sel(comparator_1_eq));  // open: en
endmodule
