// Logisim project El mallor meirdon de ejercicio que hice en mi vida. Ej 6.circ as structural Verilog: 5 circuits, main circuit main
module main (
  input  in_1,
  input  in_2,
  input  in_3,
  input  in_4,
  input  in_5,
  output out_6
);

  wire and_1_out, comparator_1_eq, comparator_1_gt, comparator_2_eq, comparator_2_gt, or_1_out;
  wire [3:0] sumador_votos_afirmativos_1_out_6, sumador_votos_con_peso_1_out_6;

  sumador_votos_con_peso sumador_votos_con_peso_1 (
    .in_1(in_1), .in_2(in_2), .in_3(in_3), .in_4(in_4), .in_5(in_5), .out_6(sumador_votos_con_peso_1_out_6));
  sumador_votos_afirmativos sumador_votos_afirmativos_1 (
    .in_1(in_1), .in_2(in_2), .in_3(in_3), .in_4(in_4), .in_5(in_5), .out_6(sumador_votos_afirmativos_1_out_6));
  Comparator #(.width(4), .mode("unsigned")) comparator_1 (
    .a(sumador_votos_afirmativos_1_out_6), .b(4'b0011), .gt(comparator_1_gt), .eq(comparator_1_eq));  // open: lt
  Comparator #(.width(4), .mode("unsigned")) comparator_2 (
    .a(sumador_votos_con_peso_1_out_6), .b(4'b0101), .gt(comparator_2_gt), .eq(comparator_2_eq));  // open: lt
  or or_1 (or_1_out, comparator_1_gt, comparator_1_eq);
  and and_1 (and_1_out, comparator_2_eq, or_1_out);
  or or_2 (out_6, comparator_2_gt, and_1_out);

  // Notes on the sheet:
  //   Presidente
  //   Secretario
  //   Consejero 1
  //   Consejero 2
  //   Consejero 3
endmodule

module full_adder (
  input  in_1,
  input  in_2,
  input  in_3,
  output out_4,
  output out_5
);

  wire and_1_out, and_2_out, and_3_out, and_4_out, and_5_out, and_6_out, and_7_out, not_1_out, not_2_out,
       not_3_out;

  not not_1 (not_1_out, in_2);
  not not_2 (not_2_out, in_3);
  not not_3 (not_3_out, in_1);
  and and_1 (and_1_out, in_2, not_2_out, not_3_out);
  and and_2 (and_2_out, in_2, in_3, in_1);
  and and_3 (and_3_out, not_1_out, in_3, not_3_out);
  and and_4 (and_4_out, not_1_out, not_2_out, in_1);
  and and_5 (and_5_out, in_3, in_1);
  and and_6 (and_6_out, in_1, in_2);
  and and_7 (and_7_out, in_3, in_2);
  or or_1 (out_4, and_5_out, and_6_out, and_7_out);
  or or_2 (out_5, and_1_out, and_2_out, and_3_out, and_4_out);
endmodule

module sumador_votos_con_peso (
  input  in_1,
  input  in_2,
  input  in_3,
  input  in_4,
  input  in_5,
  output [3:0] out_6
);

  wire [3:0] multiplexer_1_out, multiplexer_2_out, multiplexer_3_out, multiplexer_4_out, multiplexer_5_out,
       sumador_4_bits_1_out_3, sumador_4_bits_2_out_3, sumador_4_bits_3_out_3;

  Multiplexer #(.width(4)) multiplexer_1 (
    .in0(4'b0000), .in1(4'b0100), .out(multiplexer_1_out), .sel(in_1));  // open: en
  Multiplexer #(.width(4)) multiplexer_2 (
    .in0(4'b0000), .in1(4'b0011), .out(multiplexer_2_out), .sel(in_2));  // open: en
  Multiplexer #(.width(4)) multiplexer_3 (
    .in0(4'b0000), .in1(4'b0001), .out(multiplexer_3_out), .sel(in_3));  // open: en
  Multiplexer #(.width(4)) multiplexer_4 (
    .in0(4'b0000), .in1(4'b0001), .out(multiplexer_4_out), .sel(in_4));  // open: en
  Multiplexer #(.width(4)) multiplexer_5 (
    .in0(4'b0000), .in1(4'b0001), .out(multiplexer_5_out), .sel(in_5));  // open: en
  sumador_4_bits sumador_4_bits_1 (.in_1(multiplexer_1_out), .in_2(multiplexer_2_out), .out_3(sumador_4_bits_1_out_3));
  sumador_4_bits sumador_4_bits_2 (
    .in_1(sumador_4_bits_1_out_3), .in_2(multiplexer_3_out), .out_3(sumador_4_bits_2_out_3));
  sumador_4_bits sumador_4_bits_3 (
    .in_1(sumador_4_bits_2_out_3), .in_2(multiplexer_4_out), .out_3(sumador_4_bits_3_out_3));
  sumador_4_bits sumador_4_bits_4 (.in_1(sumador_4_bits_3_out_3), .in_2(multiplexer_5_out), .out_3(out_6));
endmodule

module sumador_votos_afirmativos (
  input  in_1,
  input  in_2,
  input  in_3,
  input  in_4,
  input  in_5,
  output [3:0] out_6
);

  wire [3:0] multiplexer_1_out, multiplexer_2_out, multiplexer_3_out, multiplexer_4_out, multiplexer_5_out,
       sumador_4_bits_1_out_3, sumador_4_bits_2_out_3, sumador_4_bits_3_out_3;

  Multiplexer #(.width(4)) multiplexer_1 (
    .in0(4'b0000), .in1(4'b0001), .out(multiplexer_1_out), .sel(in_1));  // open: en
  Multiplexer #(.width(4)) multiplexer_2 (
    .in0(4'b0000), .in1(4'b0001), .out(multiplexer_2_out), .sel(in_2));  // open: en
  Multiplexer #(.width(4)) multiplexer_3 (
    .in0(4'b0000), .in1(4'b0001), .out(multiplexer_3_out), .sel(in_3));  // open: en
  Multiplexer #(.width(4)) multiplexer_4 (
    .in0(4'b0000), .in1(4'b0001), .out(multiplexer_4_out), .sel(in_4));  // open: en
  Multiplexer #(.width(4)) multiplexer_5 (
    .in0(4'b0000), .in1(4'b0001), .out(multiplexer_5_out), .sel(in_5));  // open: en
  sumador_4_bits sumador_4_bits_1 (.in_1(multiplexer_1_out), .in_2(multiplexer_2_out), .out_3(sumador_4_bits_1_out_3));
  sumador_4_bits sumador_4_bits_2 (
    .in_1(sumador_4_bits_1_out_3), .in_2(multiplexer_3_out), .out_3(sumador_4_bits_2_out_3));
  sumador_4_bits sumador_4_bits_3 (
    .in_1(sumador_4_bits_2_out_3), .in_2(multiplexer_4_out), .out_3(sumador_4_bits_3_out_3));
  sumador_4_bits sumador_4_bits_4 (.in_1(sumador_4_bits_3_out_3), .in_2(multiplexer_5_out), .out_3(out_6));
endmodule

module sumador_4_bits (
  input  [3:0] in_1,
  input  [3:0] in_2,
  output [3:0] out_3
);

  wire full_adder_2_out_4, full_adder_3_out_4, full_adder_4_out_4;

  full_adder full_adder_1 (.in_1(full_adder_2_out_4), .in_2(in_1[3]), .in_3(in_2[3]), .out_5(out_3[3]));  // open: out_4
  full_adder full_adder_2 (
    .in_1(full_adder_3_out_4), .in_2(in_1[2]), .in_3(in_2[2]), .out_4(full_adder_2_out_4), .out_5(out_3[2]));
  full_adder full_adder_3 (
    .in_1(full_adder_4_out_4), .in_2(in_1[1]), .in_3(in_2[1]), .out_4(full_adder_3_out_4), .out_5(out_3[1]));
  full_adder full_adder_4 (.in_1(1'b0), .in_2(in_1[0]), .in_3(in_2[0]), .out_4(full_adder_4_out_4), .out_5(out_3[0]));
endmodule
