// Logisim project Puertas Ej 7.circ as structural Verilog: 1 circuit, main circuit main
module main (
  input  [3:0] in_1,
  input  [3:0] in_2,
  output out_3
);

  wire comparator_1_eq, comparator_1_gt, comparator_2_eq, comparator_2_gt, comparator_3_eq, comparator_3_lt,
       or_1_out, or_2_out, or_3_out;
  wire [3:0] adder_1_out, adder_2_out, multiplexer_1_out;

  Comparator #(.width(4), .mode("unsigned")) comparator_1 (
    .a(in_1), .b(4'b0110), .gt(comparator_1_gt), .eq(comparator_1_eq));  // open: lt
  or or_1 (or_1_out, comparator_1_gt, comparator_1_eq);
  Multiplexer #(.width(4)) multiplexer_1 (
    .in0(4'b0000), .in1(in_1), .out(multiplexer_1_out), .sel(or_1_out));  // open: en
  Adder #(.width(4)) adder_1 (.a({1'b0, multiplexer_1_out[3:1]}), .b(4'b1101), .out(adder_1_out));  // open: cin, cout
  Adder #(.width(4)) adder_2 (.a({1'b0, multiplexer_1_out[3:1]}), .b(4'b0011), .out(adder_2_out));  // open: cin, cout
  Comparator #(.width(4), .mode("unsigned")) comparator_2 (
    .a(in_2), .b(adder_1_out), .gt(comparator_2_gt), .eq(comparator_2_eq));  // open: lt
  Comparator #(.width(4), .mode("unsigned")) comparator_3 (
    .a(in_2), .b(adder_2_out), .eq(comparator_3_eq), .lt(comparator_3_lt));  // open: gt
  or or_2 (or_2_out, comparator_2_gt, comparator_2_eq);
  or or_3 (or_3_out, comparator_3_eq, comparator_3_lt);
  and and_1 (out_3, or_2_out, or_3_out);
endmodule
