// Logisim project Sumador BCD Ej 1-2.circ as structural Verilog: 2 circuits, main circuit main
module main (
  input  [3:0] _6,
  input  [3:0] A,
  input  [3:0] B,
  output [4:0] R
);

  wire and_1_out, and_2_out, or_1_out;
  wire [3:0] adder_1_out, adder_2_out;

  Adder #(.width(4)) adder_1 (.a(A), .b(B), .out(adder_1_out));  // open: cin, cout
  Adder #(.width(4)) adder_2 (.a(_6), .b(adder_1_out), .out(adder_2_out), .cout(R[4]));  // open: cin
  and and_1 (and_1_out, adder_1_out[1], adder_1_out[3]);
  and and_2 (and_2_out, adder_1_out[2], adder_1_out[3]);
  Multiplexer #(.width(4)) multiplexer_1 (
    .in0(adder_1_out), .in1(adder_2_out), .out(R[3:0]), .sel(or_1_out));  // open: en
  or or_1 (or_1_out, and_1_out, and_2_out);

  // Notes on the sheet:
  //   SUMADOR BCD
endmodule

module FUNCION (
  input  [3:0] in_1,
  input  [3:0] in_2,
  input  [3:0] in_3,
  output [4:0] out_4
);

  wire comparator_1_gt;
  wire [3:0] multiplexer_1_out;

  Comparator #(.width(4), .mode("unsigned")) comparator_1 (.a(in_2), .b(in_3), .gt(comparator_1_gt));  // open: eq, lt
  Multiplexer #(.width(4)) multiplexer_1 (
    .in0(in_2), .in1(in_3), .out(multiplexer_1_out), .sel(comparator_1_gt));  // open: en
  main main_1 (._6(in_1), .A(in_1), .B(multiplexer_1_out), .R(out_4));
endmodule
