// Logisim project SumadorRestadorC1C2 Ej 3.circ as structural Verilog: 1 circuit, main circuit main
module main (
  input  C1_C2,
  input  S_R,
  input  [3:0] A,
  input  [3:0] B,
  output [3:0] out_5,
  output out_6
);

  wire and_1_out, and_2_out, and_3_out, and_4_out, not_1_out, not_2_out, not_3_out, not_4_out;
  wire [3:0] xor_1_out;

  xor xor_1 (xor_1_out[0], B[0], S_R);
  xor xor_2 (xor_1_out[1], B[1], S_R);
  xor xor_3 (xor_1_out[2], B[2], S_R);
  xor xor_4 (xor_1_out[3], B[3], S_R);
  and and_1 (and_1_out, 1'b1, C1_C2);
  Adder #(.width(4)) adder_1 (.a(A), .b(xor_1_out), .out(out_5), .cin(and_1_out));  // open: cout
  not not_1 (not_1_out, S_R);
  not not_2 (not_2_out, B[3]);
  not not_3 (not_3_out, out_5[3]);
  not not_4 (not_4_out, A[3]);
  and and_2 (and_2_out, out_5[3], not_4_out, not_1_out, not_2_out);
  and and_3 (and_3_out, not_3_out, not_1_out, B[3]);
  and and_4 (and_4_out, not_2_out, not_3_out, S_R, A[3]);
  or or_1 (out_6, and_2_out, and_3_out, and_4_out);
endmodule
