// Logisim project Ejercicio 2 2010 comaprador c2.circ as structural Verilog: 1 circuit, main circuit main
module main (
  input  [3:0] in_1,
  input  [3:0] in_2,
  output out_3,
  output out_4,
  output out_5
);

  wire comparator_1_gt, comparator_1_lt, xor_1_out;

  xor xor_1 (xor_1_out, in_1[3], in_2[3]);
  Comparator #(.width(4), .mode("unsigned")) comparator_1 (
    .a(in_1), .b(in_2), .gt(comparator_1_gt), .eq(out_4), .lt(comparator_1_lt));
  xor xor_2 (out_3, xor_1_out, comparator_1_gt);
  xor xor_3 (out_5, xor_1_out, comparator_1_lt);
endmodule
