// Logisim project Ejercicio 7 2010 moore.circ as structural Verilog: 1 circuit, main circuit main
module main (
  input  in_1,
  input  in_2,
  output out_3
);

  wire and_1_out, and_2_out, button_1_out, or_1_out;

  Button button_1 (.out(button_1_out));
  D_Flip_Flop d_ff_1 (.clk(button_1_out), .D(or_1_out), .Q(out_3));  // open: Qn, preset, en, reset
  and and_1 (and_1_out, out_3, in_2);
  and and_2 (and_2_out, in_1, in_2);
  or or_1 (or_1_out, and_1_out, and_2_out);
endmodule
