// Logisim project Ejercicio 2 2013 mealy jodidisimo.circ as structural Verilog: 1 circuit, main circuit main
module main (
  input  in_1,
  output out_2
);

  wire and_1_out, and_2_out, and_3_out, and_4_out, and_5_out, button_1_out, d_ff_1_q, d_ff_2_q, d_ff_2_qn,
       d_ff_3_q, or_1_out;

  Button button_1 (.out(button_1_out));
  D_Flip_Flop d_ff_1 (.clk(button_1_out), .D(and_1_out), .Q(d_ff_1_q));  // open: Qn, preset, en, reset
  D_Flip_Flop d_ff_2 (.clk(button_1_out), .D(in_1), .Q(d_ff_2_q), .Qn(d_ff_2_qn));  // open: preset, en, reset
  D_Flip_Flop d_ff_3 (.clk(button_1_out), .D(or_1_out), .Q(d_ff_3_q));  // open: Qn, preset, en, reset
  and and_1 (and_1_out, d_ff_2_q, ~in_1);  // AND_Gate
  and and_2 (and_2_out, d_ff_2_qn, d_ff_3_q);
  and and_3 (and_3_out, d_ff_2_qn, ~in_1);  // AND_Gate
  and and_4 (and_4_out, d_ff_1_q, in_1);
  and and_5 (and_5_out, ~in_1, d_ff_3_q, d_ff_2_q);  // AND_Gate
  or or_1 (or_1_out, d_ff_1_q, and_2_out, and_3_out);
  or or_2 (out_2, and_4_out, and_5_out);
endmodule
