// Logisim project Ejericicio 1 2013 contador.circ as structural Verilog: 1 circuit, main circuit main
module main (
  input  in_1,
  input  in_2,
  input  in_3,
  input  borrar,
  input  cargar
);

  wire and_1_out, and_2_out, and_3_out, and_4_out, and_5_out, and_6_out, and_7_out, button_1_out, j_k_ff_2_q,
       j_k_ff_3_q, or_1_out, or_2_out, or_3_out;

  Button button_1 (.out(button_1_out));
  and and_1 (and_1_out, in_2, cargar);
  J_K_Flip_Flop j_k_ff_1 (
    .J(and_7_out), .clk(button_1_out), .K(and_7_out), .preset(and_1_out), .reset(or_1_out));  // open: Q, Qn, en
  or or_1 (or_1_out, borrar, and_2_out);
  and and_2 (and_2_out, ~in_2, cargar);  // AND_Gate
  J_K_Flip_Flop j_k_ff_2 (
    .J(j_k_ff_3_q), .clk(button_1_out), .K(j_k_ff_3_q), .Q(j_k_ff_2_q), .preset(and_3_out), .reset(or_2_out));  // open: Qn, en
  and and_3 (and_3_out, in_1, cargar);
  or or_2 (or_2_out, borrar, and_4_out);
  and and_4 (and_4_out, ~in_1, cargar);  // AND_Gate
  J_K_Flip_Flop j_k_ff_3 (
    .J(1'b1), .clk(button_1_out), .K(1'b1), .Q(j_k_ff_3_q), .preset(and_5_out), .reset(or_3_out));  // open: Qn, en
  and and_5 (and_5_out, in_3, cargar);
  or or_3 (or_3_out, borrar, and_6_out);
  and and_6 (and_6_out, ~in_3, cargar);  // AND_Gate
  and and_7 (and_7_out, j_k_ff_3_q, j_k_ff_2_q);
endmodule
