// Logisim project Ejercicio 2 2019 mealy.circ as structural Verilog: 1 circuit, main circuit main
module main (
  input  [1:0] in_1,
  output out_2
);

  wire and_1_out, and_2_out, and_3_out, button_1_out, d_ff_1_q, d_ff_1_qn, d_ff_2_q, not_1_out, not_2_out,
       not_3_out, not_4_out, not_5_out, not_6_out, or_1_out;

  Button button_1 (.out(button_1_out));
  D_Flip_Flop d_ff_1 (.clk(button_1_out), .D(and_1_out), .Q(d_ff_1_q), .Qn(d_ff_1_qn));  // open: preset, en, reset
  D_Flip_Flop d_ff_2 (.clk(button_1_out), .D(or_1_out), .Q(d_ff_2_q));  // open: Qn, preset, en, reset
  and and_1 (and_1_out, d_ff_1_qn, d_ff_2_q, not_1_out, in_1[0]);
  not not_1 (not_1_out, in_1[1]);
  not not_2 (not_2_out, in_1[0]);
  and and_2 (and_2_out, d_ff_1_qn, not_2_out, not_3_out);
  not not_3 (not_3_out, in_1[1]);
  and and_3 (and_3_out, d_ff_1_qn, d_ff_2_q, not_4_out);
  not not_4 (not_4_out, in_1[1]);
  and and_4 (out_2, d_ff_1_q, not_5_out, not_6_out);
  not not_5 (not_5_out, in_1[1]);
  not not_6 (not_6_out, in_1[0]);
  or or_1 (or_1_out, and_2_out, and_3_out);
endmodule
