// Logisim project Ejercicio 3 2019 T a JK.circ as structural Verilog: 1 circuit, main circuit main
module main (
  input  J,
  input  K
);

  wire and_1_out, and_2_out, button_1_out, or_1_out, t_ff_1_q, t_ff_1_qn;

  and and_1 (and_1_out, t_ff_1_q, K);
  and and_2 (and_2_out, J, t_ff_1_qn);
  Button button_1 (.out(button_1_out));
  or or_1 (or_1_out, and_1_out, and_2_out);
  T_Flip_Flop t_ff_1 (.clk(button_1_out), .T(or_1_out), .Q(t_ff_1_q), .Qn(t_ff_1_qn));  // open: preset, reset, en
endmodule
