// Logisim project Ejercicio 4 2019 contador .circ as structural Verilog: 1 circuit, main circuit main
module main (
  output [1:0] out_1
);

  wire and_1_out, and_2_out, and_3_out, and_4_out, and_5_out, and_6_out, and_7_out, and_8_out, and_9_out,
       and_10_out, button_1_out, d_ff_1_q, d_ff_1_qn, d_ff_3_qn, or_1_out, xor_1_out;
  wire [1:0] counter_1_q;

  Button button_1 (.out(button_1_out));
  and and_1 (and_1_out, and_9_out, 1'b0);
  D_Flip_Flop d_ff_1 (
    .clk(button_1_out), .D(and_10_out), .Q(d_ff_1_q), .Qn(d_ff_1_qn), .preset(and_1_out), .reset(and_2_out));  // open: en
  and and_2 (and_2_out, and_9_out, ~1'b0);  // AND_Gate
  and and_3 (and_3_out, and_9_out, counter_1_q[1]);
  D_Flip_Flop d_ff_2 (
    .clk(button_1_out), .D(xor_1_out), .Q(out_1[1]), .preset(and_3_out), .reset(and_4_out));  // open: Qn, en
  and and_4 (and_4_out, and_9_out, ~counter_1_q[1]);  // AND_Gate
  D_Flip_Flop d_ff_3 (
    .clk(button_1_out), .D(or_1_out), .Q(out_1[0]), .Qn(d_ff_3_qn), .preset(and_5_out), .reset(and_6_out));  // open: en
  and and_5 (and_5_out, and_9_out, counter_1_q[0]);
  and and_6 (and_6_out, and_9_out, ~counter_1_q[0]);  // AND_Gate
  and and_7 (and_7_out, out_1[1], d_ff_3_qn);
  and and_8 (and_8_out, d_ff_3_qn, d_ff_1_qn);
  and and_9 (and_9_out, ~out_1[0], ~out_1[1], d_ff_1_q);  // AND_Gate
  xor xor_1 (xor_1_out, out_1[1], out_1[0]);
  and and_10 (and_10_out, out_1[1], out_1[0]);
  or or_1 (or_1_out, and_7_out, and_8_out);
  Counter #(.width(2), .max('h3)) counter_1 (.Q(counter_1_q), .clk(and_9_out));  // open: load, D, count, carry, clr
endmodule
