// Logisim project Ejercicio 2 2022 mealy.circ as structural Verilog: 1 circuit, main circuit main
module main (
  input  [1:0] in_1,
  output out_2
);

  wire and_1_out, and_3_out, button_1_out, d_ff_1_q, d_ff_1_qn, d_ff_2_q, d_ff_2_qn, not_1_out, or_1_out;

  Button button_1 (.out(button_1_out));
  D_Flip_Flop d_ff_1 (.clk(button_1_out), .D(and_1_out), .Q(d_ff_1_q), .Qn(d_ff_1_qn));  // open: preset, en, reset
  not not_1 (not_1_out, in_1[1]);
  D_Flip_Flop d_ff_2 (.clk(button_1_out), .D(or_1_out), .Q(d_ff_2_q), .Qn(d_ff_2_qn));  // open: preset, en, reset
  and and_1 (and_1_out, d_ff_1_qn, d_ff_2_q, in_1[0], in_1[1]);
  and and_2 (out_2, in_1[0], d_ff_1_q, in_1[1]);
  and and_3 (and_3_out, d_ff_1_qn, d_ff_2_q, in_1[0]);
  or or_1 (or_1_out, not_1_out, and_3_out);
endmodule
