// Logisim project Ejercicio 3 2022 contador.circ as structural Verilog: 1 circuit, main circuit main
module main (
  input  in_1,
  input  in_2,
  input  in_3,
  input  in_4
);

  wire and_1_out, button_1_out, j_k_ff_1_q, j_k_ff_1_qn, j_k_ff_2_q, j_k_ff_2_qn, j_k_ff_3_q,
       multiplexer_1_out, multiplexer_2_out, multiplexer_3_out, multiplexer_4_out, multiplexer_5_out,
       multiplexer_6_out, not_1_out, not_2_out, not_3_out, or_1_out, or_2_out;

  Button button_1 (.out(button_1_out));
  Multiplexer multiplexer_1 (.in0(and_1_out), .in1(in_2), .out(multiplexer_1_out), .sel(in_1));  // open: en
  Multiplexer multiplexer_2 (.in0(j_k_ff_2_q), .in1(not_1_out), .out(multiplexer_2_out), .sel(in_1));  // open: en
  not not_1 (not_1_out, in_2);
  J_K_Flip_Flop j_k_ff_1 (
    .J(multiplexer_1_out), .clk(button_1_out), .K(multiplexer_2_out), .Q(j_k_ff_1_q), .Qn(j_k_ff_1_qn));  // open: preset, en, reset
  not not_2 (not_2_out, in_3);
  Multiplexer multiplexer_3 (.in0(j_k_ff_3_q), .in1(in_3), .out(multiplexer_3_out), .sel(in_1));  // open: en
  Multiplexer multiplexer_4 (.in0(or_2_out), .in1(not_2_out), .out(multiplexer_4_out), .sel(in_1));  // open: en
  J_K_Flip_Flop j_k_ff_2 (
    .J(multiplexer_3_out), .clk(button_1_out), .K(multiplexer_4_out), .Q(j_k_ff_2_q), .Qn(j_k_ff_2_qn));  // open: preset, en, reset
  not not_3 (not_3_out, in_4);
  Multiplexer multiplexer_5 (.in0(or_1_out), .in1(in_4), .out(multiplexer_5_out), .sel(in_1));  // open: en
  Multiplexer multiplexer_6 (.in0(1'b1), .in1(not_3_out), .out(multiplexer_6_out), .sel(in_1));  // open: en
  J_K_Flip_Flop j_k_ff_3 (
    .J(multiplexer_5_out), .clk(button_1_out), .K(multiplexer_6_out), .Q(j_k_ff_3_q));  // open: Qn, preset, en, reset
  or or_1 (or_1_out, j_k_ff_1_qn, j_k_ff_2_qn);
  and and_1 (and_1_out, j_k_ff_3_q, j_k_ff_2_q);
  or or_2 (or_2_out, j_k_ff_3_q, j_k_ff_1_q);
endmodule
