// Logisim project Ejercicio 4 2022 comparador con reloj.circ as structural Verilog: 1 circuit, main circuit main
module main (
  input  [3:0] in_1,
  input  [3:0] in_2,
  output out_3,
  output [3:0] out_4
);

  wire button_1_out, comparator_1_gt, counter_1_q, xor_1_out, xor_2_out;
  wire [3:0] adder_1_out, multiplexer_1_out;

  Multiplexer #(.width(4)) multiplexer_1 (
    .in0(in_2), .in1(in_1), .out(multiplexer_1_out), .sel(xor_2_out));  // open: en
  xor xor_1 (xor_1_out, in_1[3], in_2[3]);
  Comparator #(.width(4), .mode("unsigned")) comparator_1 (.a(in_1), .b(in_2), .gt(comparator_1_gt));  // open: eq, lt
  xor xor_2 (xor_2_out, xor_1_out, comparator_1_gt);
  Adder #(.width(4)) adder_1 (.a(multiplexer_1_out), .b(4'b0000), .out(adder_1_out), .cin(1'b1));  // open: cout
  Button button_1 (.out(button_1_out));
  Counter #(.width(1), .max('h1)) counter_1 (.Q(counter_1_q), .clk(button_1_out));  // open: load, D, count, carry, clr
  Multiplexer #(.width(4)) multiplexer_2 (
    .in0(adder_1_out), .in1(4'b0000), .out(out_4), .sel(counter_1_q));  // open: en
  xor xor_3 (out_3, multiplexer_1_out[3], adder_1_out[3]);
endmodule
