// Logisim project Ejercicio 3 2023 contador.circ as structural Verilog: 1 circuit, main circuit main
module main (
);

  wire and_1_out, and_2_out, and_3_out, and_4_out, and_5_out, and_6_out, and_9_out, button_1_out, j_k_ff_1_q,
       j_k_ff_2_q, j_k_ff_3_q, or_1_out;
  wire [1:0] and_7_out;
  wire [2:0] multiplexer_1_out;

  Button button_1 (.out(button_1_out));
  J_K_Flip_Flop j_k_ff_1 (
    .J(and_9_out), .clk(button_1_out), .K(and_9_out), .Q(j_k_ff_1_q), .preset(and_2_out), .reset(and_1_out));  // open: Qn, en
  and and_1 (and_1_out, or_1_out, ~multiplexer_1_out[2]);  // AND_Gate
  and and_2 (and_2_out, or_1_out, multiplexer_1_out[2]);
  and and_3 (and_3_out, or_1_out, multiplexer_1_out[1]);
  J_K_Flip_Flop j_k_ff_2 (
    .J(j_k_ff_3_q), .clk(button_1_out), .K(j_k_ff_3_q), .Q(j_k_ff_2_q), .preset(and_3_out), .reset(and_4_out));  // open: Qn, en
  and and_4 (and_4_out, or_1_out, ~multiplexer_1_out[1]);  // AND_Gate
  and and_5 (and_5_out, or_1_out, multiplexer_1_out[0]);
  J_K_Flip_Flop j_k_ff_3 (
    .J(1'b1), .clk(button_1_out), .K(1'b1), .Q(j_k_ff_3_q), .preset(and_5_out), .reset(and_6_out));  // open: Qn, en
  and and_6 (and_6_out, or_1_out, ~multiplexer_1_out[0]);  // AND_Gate
  and and_7 (and_7_out[0], ~j_k_ff_1_q, j_k_ff_2_q, j_k_ff_3_q);  // AND_Gate
  and and_8 (and_7_out[1], j_k_ff_1_q, j_k_ff_2_q, ~j_k_ff_3_q);  // AND_Gate
  and and_9 (and_9_out, j_k_ff_3_q, j_k_ff_2_q);
  or or_1 (or_1_out, and_7_out[0], and_7_out[1]);
  Multiplexer #(.select(2), .width(3)) multiplexer_1 (
    .in1(3'b101), .in2(3'b111), .out(multiplexer_1_out), .sel(and_7_out));  // open: in0, in3, en
endmodule
