// Logisim project Ejericio  5 2023 comparador c1.circ as structural Verilog: 1 circuit, main circuit main
module main (
  input  [3:0] in_1,
  input  [3:0] in_2,
  output out_3,
  output out_4,
  output out_5
);

  wire and_1_out, and_2_out, comparator_1_gt, comparator_1_lt, xor_9_out;
  wire [3:0] xor_1_out, xor_5_out;

  and and_1 (and_1_out, in_1[0], in_1[1], in_1[2], in_1[3]);
  and and_2 (and_2_out, in_2[0], in_2[1], in_2[2], in_2[3]);
  xor xor_1 (xor_1_out[0], in_1[0], and_1_out);
  xor xor_2 (xor_1_out[1], in_1[1], and_1_out);
  xor xor_3 (xor_1_out[2], in_1[2], and_1_out);
  xor xor_4 (xor_1_out[3], in_1[3], and_1_out);
  xor xor_5 (xor_5_out[0], in_2[0], and_2_out);
  xor xor_6 (xor_5_out[1], in_2[1], and_2_out);
  xor xor_7 (xor_5_out[2], in_2[2], and_2_out);
  xor xor_8 (xor_5_out[3], in_2[3], and_2_out);
  xor xor_9 (xor_9_out, xor_1_out[3], xor_5_out[3]);
  Comparator #(.width(4), .mode("unsigned")) comparator_1 (
    .a(xor_1_out), .b(xor_5_out), .gt(comparator_1_gt), .eq(out_4), .lt(comparator_1_lt));
  xor xor_10 (out_3, xor_9_out, comparator_1_gt);
  xor xor_11 (out_5, comparator_1_lt, xor_9_out);
endmodule
