// Logisim project Ejercicio 3 2024 comparador.circ as structural Verilog: 1 circuit, main circuit main
module main (
  input  [3:0] in_1,
  input  in_2,
  input  [3:0] in_3,
  output out_4,
  output out_5,
  output out_6
);

  wire and_1_out, and_2_out, and_3_out, and_4_out, and_5_out, and_6_out, and_7_out, comparator_1_gt,
       comparator_1_lt, or_1_out, or_2_out, or_3_out;
  wire [3:0] xor_1_out, xor_5_out;

  and and_1 (and_1_out, ~in_1[0], ~in_1[1], ~in_1[2], in_1[3], ~in_2);  // AND_Gate
  and and_2 (and_2_out, ~in_3[0], ~in_3[1], ~in_3[2], in_3[3], ~in_2);  // AND_Gate
  and and_3 (and_3_out, in_2, in_1[0], in_1[1], in_1[2], in_1[3]);
  and and_4 (and_4_out, in_2, in_3[0], in_3[1], in_3[2], in_3[3]);
  or or_1 (or_1_out, and_1_out, and_3_out);
  or or_2 (or_2_out, and_2_out, and_4_out);
  xor xor_1 (xor_1_out[0], in_1[0], and_3_out);
  xor xor_2 (xor_1_out[1], in_1[1], and_3_out);
  xor xor_3 (xor_1_out[2], in_1[2], and_3_out);
  xor xor_4 (xor_1_out[3], in_1[3], or_1_out);
  xor xor_5 (xor_5_out[0], in_3[0], and_4_out);
  xor xor_6 (xor_5_out[1], in_3[1], and_4_out);
  xor xor_7 (xor_5_out[2], in_3[2], and_4_out);
  xor xor_8 (xor_5_out[3], in_3[3], or_2_out);
  and and_5 (and_5_out, ~in_2, xor_1_out[3]);  // AND_Gate
  and and_6 (and_6_out, ~xor_1_out[3], xor_5_out[3]);  // AND_Gate
  or or_3 (or_3_out, and_5_out, and_6_out, and_7_out);
  and and_7 (and_7_out, ~xor_5_out[3], xor_1_out[3]);  // AND_Gate
  Comparator #(.width(4), .mode("unsigned")) comparator_1 (
    .a(xor_1_out), .b(xor_5_out), .gt(comparator_1_gt), .eq(out_5), .lt(comparator_1_lt));
  xor xor_9 (out_4, or_3_out, comparator_1_gt);
  xor xor_10 (out_6, or_3_out, comparator_1_lt);
endmodule
