// Logisim project Ejercicio 4 2024 contador.circ as structural Verilog: 1 circuit, main circuit main
module main (
  input  in_1,
  input  in_2,
  input  L0,
  input  L1,
  output [1:0] out_5
);

  wire button_1_out, multiplexer_1_out, multiplexer_2_out, multiplexer_3_out, multiplexer_4_out, not_1_out,
       not_2_out;

  Button button_1 (.out(button_1_out));
  not not_1 (not_1_out, L1);
  Multiplexer #(.select(2)) multiplexer_1 (
    .in0(1'b1), .in1(L1), .in2(1'b0), .out(multiplexer_1_out), .sel({in_1, in_2}));  // open: in3, en
  Multiplexer #(.select(2)) multiplexer_2 (
    .in0(1'b1), .in1(not_1_out), .in2(1'b1), .out(multiplexer_2_out), .sel({in_1, in_2}));  // open: in3, en
  J_K_Flip_Flop j_k_ff_1 (
    .J(multiplexer_1_out), .clk(button_1_out), .K(multiplexer_2_out), .Q(out_5[1]));  // open: Qn, preset, en, reset
  not not_2 (not_2_out, L0);
  Multiplexer #(.select(2)) multiplexer_3 (
    .in0(out_5[1]), .in1(L0), .in2(1'b0), .out(multiplexer_3_out), .sel({in_1, in_2}));  // open: in3, en
  Multiplexer #(.select(2)) multiplexer_4 (
    .in0(out_5[1]), .in1(not_2_out), .in2(1'b1), .out(multiplexer_4_out), .sel({in_1, in_2}));  // open: in3, en
  J_K_Flip_Flop j_k_ff_2 (
    .J(multiplexer_3_out), .clk(button_1_out), .K(multiplexer_4_out), .Q(out_5[0]));  // open: Qn, preset, en, reset

  // Notes on the sheet:
  //   00 SECUENCIA NORMAL
  //   01 CARGA
  //   10 DESCARGA
endmodule
