// Logisim project Ejericio 2 2024 mealy.circ as structural Verilog: 1 circuit, main circuit main
module main (
  input  in_1,
  output out_2
);

  wire and_2_out, button_1_out, d_ff_1_q, d_ff_2_q;

  Button button_1 (.out(button_1_out));
  D_Flip_Flop d_ff_1 (.clk(button_1_out), .D(and_2_out), .Q(d_ff_1_q));  // open: Qn, preset, en, reset
  D_Flip_Flop d_ff_2 (.clk(button_1_out), .D(in_1), .Q(d_ff_2_q));  // open: Qn, preset, en, reset
  and and_1 (out_2, d_ff_1_q, in_1);
  and and_2 (and_2_out, in_1, d_ff_2_q);
endmodule
