// Logisim project Comparador c2.circ as structural Verilog: 1 circuit, main circuit main
module main (
  input  [3:0] in_1,
  input  [3:0] in_2,
  output [3:0] out_3
);

  wire comparator_1_gt, xor_1_out, xor_2_out;

  xor xor_1 (xor_1_out, in_1[3], in_2[3]);
  Comparator #(.width(4), .mode("unsigned")) comparator_1 (.a(in_1), .b(in_2), .gt(comparator_1_gt));  // open: eq, lt
  xor xor_2 (xor_2_out, xor_1_out, comparator_1_gt);
  Multiplexer #(.width(4)) multiplexer_1 (.in0(in_2), .in1(in_1), .out(out_3), .sel(xor_2_out));  // open: en
endmodule
