// Logisim project Comparadro sumador.circ as structural Verilog: 1 circuit, main circuit main
module main (
  input  [5:0] in_1,
  output [5:0] out_2
);

  wire comparator_1_eq, comparator_1_gt, xor_1_out, xor_2_out;
  wire [5:0] multiplexer_1_out, multiplexer_2_out;

  xor xor_1 (xor_1_out, in_1[5], 1'b0);
  Comparator #(.width(6), .mode("unsigned")) comparator_1 (
    .a(in_1), .b({6{1'b0}}), .gt(comparator_1_gt), .eq(comparator_1_eq));  // open: lt
  xor xor_2 (xor_2_out, xor_1_out, comparator_1_gt);
  Multiplexer #(.width(6)) multiplexer_1 (
    .in0(6'b000011), .in1(6'b111101), .out(multiplexer_1_out), .sel(xor_2_out));  // open: en
  Multiplexer #(.width(6)) multiplexer_2 (
    .in0(multiplexer_1_out), .in1({6{1'b0}}), .out(multiplexer_2_out), .sel(comparator_1_eq));  // open: en
  Adder #(.width(6)) adder_1 (.a(in_1), .b(multiplexer_2_out), .out(out_2));  // open: cin, cout
endmodule
