// Logisim project Divisor restador.circ as structural Verilog: 1 circuit, main circuit main
module main (
  input  [3:0] in_1,
  input  [3:0] in_2,
  output [3:0] out_3,
  output [3:0] out_4
);

  wire [0:0] adder_1_out;
  wire [3:0] xor_1_out;

  Adder #(.width(4)) adder_1 (.a(in_1), .b(in_2), .out({out_3[2:0], adder_1_out[0]}));  // open: cin, cout
  xor xor_1 (xor_1_out[0], in_2[0], 1'b1);
  xor xor_2 (xor_1_out[1], in_2[1], 1'b1);
  xor xor_3 (xor_1_out[2], 1'b1, in_2[2]);
  xor xor_4 (xor_1_out[3], 1'b1, in_2[3]);
  Adder #(.width(4)) adder_2 (.a(in_1), .b(xor_1_out), .out(out_4), .cin(1'b1));  // open: cout

  assign out_3[3] = 1'b0;
endmodule
