// Logisim project Registro comparador.circ as structural Verilog: 1 circuit, main circuit main
module main (
  input  [3:0] in_1,
  output [3:0] out_2
);

  wire and_1_out, and_2_out, and_3_out, and_4_out, and_5_out, and_6_out, and_7_out, and_8_out, and_9_out,
       and_10_out, button_1_out, comparator_1_lt, or_1_out, or_2_out, or_3_out, or_4_out, xor_1_out,
       xor_2_out;
  wire [2:0] counter_1_q;
  wire [3:0] d_ff_4_q;

  Button button_1 (.out(button_1_out));
  Counter #(.width(3), .max('h7)) counter_1 (.Q(counter_1_q), .clk(button_1_out));  // open: load, D, count, carry, clr
  and and_1 (and_1_out, ~counter_1_q[0], ~counter_1_q[1], ~counter_1_q[2]);  // AND_Gate
  D_Flip_Flop d_ff_1 (.Q(d_ff_4_q[3]), .preset(and_3_out), .reset(or_1_out));  // open: clk, D, Qn, en
  or or_1 (or_1_out, and_1_out, and_2_out);
  and and_2 (and_2_out, ~in_1[3], and_10_out);  // AND_Gate
  and and_3 (and_3_out, and_10_out, in_1[3]);
  xor xor_1 (xor_1_out, in_1[3], d_ff_4_q[3]);
  or or_2 (or_2_out, and_1_out, and_4_out);
  and and_4 (and_4_out, and_10_out, in_1[2]);
  D_Flip_Flop d_ff_2 (.Q(d_ff_4_q[2]), .preset(or_2_out), .reset(and_5_out));  // open: clk, D, Qn, en
  and and_5 (and_5_out, ~in_1[2], and_10_out);  // AND_Gate
  and and_6 (and_6_out, and_10_out, in_1[1]);
  D_Flip_Flop d_ff_3 (.Q(d_ff_4_q[1]), .preset(or_3_out), .reset(and_7_out));  // open: clk, D, Qn, en
  or or_3 (or_3_out, and_1_out, and_6_out);
  and and_7 (and_7_out, ~in_1[1], and_10_out);  // AND_Gate
  D_Flip_Flop d_ff_4 (.Q(d_ff_4_q[0]), .preset(or_4_out), .reset(and_8_out));  // open: clk, D, Qn, en
  or or_4 (or_4_out, and_1_out, and_9_out);
  and and_8 (and_8_out, ~in_1[0], and_10_out);  // AND_Gate
  and and_9 (and_9_out, and_10_out, in_1[0]);
  Comparator #(.width(4), .mode("unsigned")) comparator_1 (
    .a(in_1), .b(d_ff_4_q), .lt(comparator_1_lt));  // open: gt, eq
  xor xor_2 (xor_2_out, xor_1_out, comparator_1_lt);
  Multiplexer #(.select(3), .width(4)) multiplexer_1 (
    .in7(d_ff_4_q), .out(out_2), .sel(counter_1_q));  // open: in0, in1, in2, in3, in4, in5, in6, en
  and and_10 (and_10_out, xor_2_out, button_1_out);
endmodule
